// Logisim project Implementation.circ as structural Verilog: 4 circuits, main circuit main
module main (
);


  // Notes on the sheet:
  //   Click 8 bit for 8 bit word prototype
  //   Click 16 bit for 16 bit word prototype
endmodule

module _8_bit (
  input  [7:0] Input_Code,
  input  W_R,
  input  [7:0] in_3,
  output [7:0] Current_Instruction,
  output [3:0] Opcode,
  output [3:0] Operand,
  output [7:0] out_7,
  output [7:0] out_8,
  output [7:0] out_9
);

  wire button_1_out, clock_1_out, demultiplexer_1_out0, demultiplexer_1_out1, demultiplexer_1_out2,
       demultiplexer_1_out3, demultiplexer_1_out4, demultiplexer_1_out5, demultiplexer_1_out15, not_1_out,
       not_2_out, not_3_out;
  wire [3:0] MAR_q, PC_q;
  wire [7:0] IN_REG_q, MBR_IN_q, MBR_q, multiplexer_1_out, multiplexer_2_out, multiplexer_3_out, ram_1_data,
       ram_2_data;

  Counter #(.width(4), .max('hf)) PC (
    .count(clock_1_out), .Q(PC_q), .clk(clock_1_out), .clr(button_1_out));  // open: load, D, carry
  Button button_1 (.out(button_1_out));
  not not_1 (not_1_out, demultiplexer_1_out15);
  Clock clock_1 (.out(clock_1_out));
  LED IDLE (.in(demultiplexer_1_out0));
  RAM #(.addrWidth(4)) ram_1 (
    .addr(PC_q), .data(ram_1_data), .sel(not_1_out), .clk(clock_1_out), .ld(W_R));  // open: clr
  not not_2 (not_2_out, W_R);
  Register IR (.D(ram_1_data), .Q(Current_Instruction), .clk(clock_1_out), .clr(not_3_out));  // open: en
  not not_3 (not_3_out, W_R);
  Demultiplexer #(.select(4), .enable("false")) demultiplexer_1 (
    .out0(demultiplexer_1_out0), .out1(demultiplexer_1_out1), .out2(demultiplexer_1_out2),
    .out3(demultiplexer_1_out3), .out4(demultiplexer_1_out4), .out5(demultiplexer_1_out5),
    .out15(demultiplexer_1_out15), .in(1'b1), .sel(Current_Instruction[7:4]));  // open: out6, out7, out8, out9, out10, out11, out12, out13, out14
  Demultiplexer #(.width(8)) demultiplexer_2 (
    .out0(ram_1_data), .in(Input_Code), .sel(1'b0), .en(not_2_out));  // open: out1
  Register #(.width(4), .trigger("high")) MAR (
    .D(Current_Instruction[3:0]), .Q(MAR_q), .clk(clock_1_out));  // open: en, clr
  RAM #(.addrWidth(4), .bus("separate")) ram_2 (
    .addr(MAR_q), .din(MBR_IN_q), .data(ram_2_data), .str(demultiplexer_1_out2), .clk(clock_1_out));  // open: sel, ld, clr
  Multiplexer #(.width(8), .enable("false")) multiplexer_1 (
    .in0(multiplexer_3_out), .in1(out_7), .out(multiplexer_1_out), .sel(demultiplexer_1_out4));
  Register #(.trigger("high")) MBR_IN (.D(out_9), .Q(MBR_IN_q), .clk(clock_1_out));  // open: en, clr
  Register #(.trigger("high")) MBR (.D(ram_2_data), .Q(MBR_q), .clk(clock_1_out));  // open: en, clr
  Multiplexer #(.width(8), .enable("false")) multiplexer_2 (
    .in0(MBR_q), .in1(IN_REG_q), .out(multiplexer_2_out), .sel(demultiplexer_1_out5));
  Register AC (.D(multiplexer_1_out), .Q(out_9), .clk(clock_1_out));  // open: en, clr
  Multiplexer #(.width(8), .enable("false")) multiplexer_3 (
    .in0(multiplexer_2_out), .in1(out_8), .out(multiplexer_3_out), .sel(demultiplexer_1_out3));
  Register IN_REG (.D(in_3), .Q(IN_REG_q), .clk(clock_1_out));  // open: en, clr
  Multiplier multiplier_1 (.a(MBR_q), .b(out_9), .out(out_7));  // open: cin, cout
  Adder adder_1 (.a(MBR_q), .b(out_9), .out(out_8));  // open: cin, cout

  assign Opcode = Current_Instruction[7:4];
  assign Operand = Current_Instruction[3:0];

  // Notes on the sheet:
  //   Control Unit
  //   CMB
  //   LOAD-0001
  //   STORE-0010
  //   INPUT-0101
  //   END-1111
  //   MM
  //   ADD-0011
  //   MUL-0100
  //   ALU
endmodule

module _16_bit (
  input  [15:0] Input_Code,
  input  W_R,
  input  [15:0] in_3,
  output [15:0] Current_Instruction,
  output [11:0] Operand,
  output [15:0] ALU,
  output [3:0] Opcode,
  output [15:0] out_8,
  output [15:0] out_9
);

  wire button_1_out, clock_1_out, demultiplexer_1_out0, demultiplexer_1_out1, demultiplexer_1_out2,
       demultiplexer_1_out3, demultiplexer_1_out4, demultiplexer_1_out5, demultiplexer_1_out15, not_1_out,
       not_2_out, not_3_out;
  wire [3:0] PC_q;
  wire [11:0] MAR_q;
  wire [15:0] IN_REG_q, MBR_IN_q, MBR_q, multiplexer_1_out, multiplexer_2_out, multiplexer_3_out, ram_1_data,
       ram_2_data;

  Counter #(.width(4), .max('hf)) PC (
    .count(clock_1_out), .Q(PC_q), .clk(clock_1_out), .clr(button_1_out));  // open: load, D, carry
  Button button_1 (.out(button_1_out));
  not not_1 (not_1_out, demultiplexer_1_out15);
  Clock clock_1 (.out(clock_1_out));
  LED IDLE (.in(demultiplexer_1_out0));
  RAM #(.addrWidth(4), .dataWidth(16)) ram_1 (
    .addr(PC_q), .data(ram_1_data), .sel(not_1_out), .clk(clock_1_out), .ld(W_R));  // open: clr
  not not_2 (not_2_out, W_R);
  Register #(.width(16)) IR (.D(ram_1_data), .Q(Current_Instruction), .clk(clock_1_out), .clr(not_3_out));  // open: en
  not not_3 (not_3_out, W_R);
  Demultiplexer #(.select(4), .enable("false")) demultiplexer_1 (
    .out0(demultiplexer_1_out0), .out1(demultiplexer_1_out1), .out2(demultiplexer_1_out2),
    .out3(demultiplexer_1_out3), .out4(demultiplexer_1_out4), .out5(demultiplexer_1_out5),
    .out15(demultiplexer_1_out15), .in(1'b1), .sel(Current_Instruction[15:12]));  // open: out6, out7, out8, out9, out10, out11, out12, out13, out14
  Demultiplexer #(.width(16)) demultiplexer_2 (
    .out0(ram_1_data), .in(Input_Code), .sel(1'b0), .en(not_2_out));  // open: out1
  Register #(.width(12), .trigger("high")) MAR (
    .D(Current_Instruction[11:0]), .Q(MAR_q), .clk(clock_1_out));  // open: en, clr
  RAM #(.addrWidth(12), .dataWidth(16), .bus("separate")) ram_2 (
    .addr(MAR_q), .din(MBR_IN_q), .data(ram_2_data), .str(demultiplexer_1_out2), .clk(clock_1_out));  // open: sel, ld, clr
  Multiplexer #(.width(16), .enable("false")) multiplexer_1 (
    .in0(multiplexer_3_out), .in1(ALU), .out(multiplexer_1_out), .sel(demultiplexer_1_out4));
  Register #(.width(16), .trigger("high")) MBR_IN (.D(out_9), .Q(MBR_IN_q), .clk(clock_1_out));  // open: en, clr
  Register #(.width(16), .trigger("high")) MBR (.D(ram_2_data), .Q(MBR_q), .clk(clock_1_out));  // open: en, clr
  Multiplexer #(.width(16), .enable("false")) multiplexer_2 (
    .in0(MBR_q), .in1(IN_REG_q), .out(multiplexer_2_out), .sel(demultiplexer_1_out5));
  Register #(.width(16)) AC (.D(multiplexer_1_out), .Q(out_9), .clk(clock_1_out));  // open: en, clr
  Multiplexer #(.width(16), .enable("false")) multiplexer_3 (
    .in0(multiplexer_2_out), .in1(out_8), .out(multiplexer_3_out), .sel(demultiplexer_1_out3));
  Register #(.width(16)) IN_REG (.D(in_3), .Q(IN_REG_q), .clk(clock_1_out));  // open: en, clr
  Multiplier #(.width(16)) multiplier_1 (.a(MBR_q), .b(out_9), .out(ALU));  // open: cin, cout
  Adder #(.width(16)) adder_1 (.a(MBR_q), .b(out_9), .out(out_8));  // open: cin, cout

  assign Opcode = Current_Instruction[15:12];
  assign Operand = Current_Instruction[11:0];

  // Notes on the sheet:
  //   Control Unit
  //   CMB
  //   LOAD-0001
  //   STORE-0010
  //   INPUT-0101
  //   END-1111
  //   MM
  //   ADD-0011
  //   MUL-0100
endmodule

module MAIN_CODE (
  input  [15:0] in_1,
  input  in_2,
  input  in_3,
  input  [3:0] in_4,
  input  in_5,
  input  [3:0] in_6,
  output [15:0] out_7,
  output [15:0] out_8
);

  wire button_1_out, button_2_out, clock_1_out, clock_2_out, not_1_out;
  wire [11:0] MAR_2_q, MAR_q, multiplexer_1_out, multiplexer_2_out, PC_2_q, PC_q;
  wire [15:0] demultiplexer_1_out0, demultiplexer_1_out1, demultiplexer_2_out0, demultiplexer_2_out1,
       MBR_prime_2_q, MBR_prime_q, ram_1_data, ram_2_data;

  Counter #(.width(12), .max('hf)) PC (.Q(PC_q), .clk(clock_1_out), .clr(in_2));  // open: load, D, count, carry
  Counter #(.width(12), .max('hf)) PC_2 (
    .Q(PC_2_q), .clk(clock_2_out), .clr(button_1_out));  // open: load, D, count, carry
  Button button_1 (.out(button_1_out));
  Multiplexer #(.width(12), .enable("false")) multiplexer_1 (
    .in0(MAR_2_q), .in1(PC_q), .out(multiplexer_1_out), .sel(clock_1_out));
  Multiplexer #(.width(12), .enable("false")) multiplexer_2 (
    .in0(MAR_q), .in1(PC_2_q), .out(multiplexer_2_out), .sel(clock_2_out));
  not not_1 (not_1_out, in_3);
  Clock clock_1 (.out(clock_1_out));
  Button button_2 (.out(button_2_out));
  Clock clock_2 (.out(clock_2_out));
  RAM #(.addrWidth(12), .dataWidth(16), .bus("separate")) ram_1 (
    .addr(multiplexer_1_out), .din(in_1), .data(ram_1_data), .str(in_3), .clk(clock_1_out), .ld(not_1_out));  // open: sel, clr
  Register #(.width(16)) IR (.D(demultiplexer_2_out0), .Q({in_4, out_7[11:0]}), .clk(clock_1_out));  // open: en, clr
  RAM #(.addrWidth(12), .dataWidth(16), .bus("asynch")) ram_2 (
    .addr(multiplexer_2_out), .data(ram_2_data), .ld(in_5), .clr(button_2_out));  // open: sel
  Demultiplexer #(.width(16), .enable("false")) demultiplexer_1 (
    .out0(demultiplexer_1_out0), .out1(demultiplexer_1_out1), .in(ram_2_data), .sel(clock_2_out));
  Register #(.width(16)) IR_2 (.D(demultiplexer_1_out0), .Q({in_6, out_8[11:0]}), .clk(clock_2_out));  // open: en, clr
  Demultiplexer #(.width(16), .enable("false")) demultiplexer_2 (
    .out0(demultiplexer_2_out0), .out1(demultiplexer_2_out1), .in(ram_1_data), .sel(clock_1_out));
  Register #(.width(12), .trigger("high")) MAR (.D(out_8[11:0]), .Q(MAR_q), .clk(clock_2_out));  // open: en, clr
  Register #(.width(16), .trigger("high")) MBR_prime (
    .D(demultiplexer_2_out1), .Q(MBR_prime_q), .clk(clock_1_out));  // open: en, clr
  Register #(.width(12), .trigger("high")) MAR_2 (.D(out_7[11:0]), .Q(MAR_2_q), .clk(clock_1_out));  // open: en, clr
  Register #(.width(16), .trigger("high")) MBR_prime_2 (
    .D(demultiplexer_1_out1), .Q(MBR_prime_2_q), .clk(clock_2_out));  // open: en, clr
  Register #(.width(16), .trigger("high")) AC (.D(MBR_prime_q), .clk(clock_1_out));  // open: en, Q, clr
  Register #(.width(16), .trigger("high")) AC_2 (.D(MBR_prime_2_q), .clk(clock_2_out));  // open: en, Q, clr

  assign out_7[15:12] = in_4;
  assign out_8[15:12] = in_6;

  // Notes on the sheet:
  //   This contains a prototype where one MM is used
  //   MM
  //   MM
endmodule
